# Fritzing sketch PoC 1 (saved by Fritzing 0.9.3b)
breadboards: 1

parts:
  Arduino_Relay_Shield_v3_0 = SeeedStudio Relay Shield 2.1
  S1 = Pushbutton [package="[SMD]"]
  S2 = Pushbutton [package="[SMD]"]
  R1 = Resistor [tolerance=±5% resistance=220 package="2010 [SMD]"]
  R2 = Resistor [tolerance=±5% resistance=220 package="2010 [SMD]"]
  R3 = Resistor [tolerance=±5% resistance=220 package="2010 [SMD]"]
  R4 = Resistor [tolerance=±5% resistance=220 package="2010 [SMD]"]
  R5 = Resistor [tolerance=±5% resistance=10k package="2010 [SMD]"]
  R6 = Resistor [tolerance=±5% resistance=10k package="2010 [SMD]"]
  LED1 = LED - 3mm [color="Green (555nm)" package="3 mm [THT]"]
  LED2 = LED - 3mm [color="Yellow (585nm)" package="3 mm [THT]"]
  LED3 = LED - 3mm [color="Red (633nm)" package="3 mm [THT]"]
  LED4 = LED - 3mm [color="Blue (430nm)" package="3 mm [THT]"]

nets:
  N1: Arduino_Relay_Shield_v3_0.5V, Arduino_Relay_Shield_v3_0.COM1, Arduino_Relay_Shield_v3_0.COM2, S1.Pin_1, S1.Pin_2, S2.Pin_1, S2.Pin_2
  N2: Arduino_Relay_Shield_v3_0.GND1, R5.Pin_1, R6.Pin_1, LED1.cathode, LED2.cathode, LED3.cathode, LED4.cathode
  N3: Arduino_Relay_Shield_v3_0.D2, S1.Pin_3, S1.Pin_4, R5.Pin_0
  N4: Arduino_Relay_Shield_v3_0.D3, S2.Pin_3, S2.Pin_4, R6.Pin_0
  N5: Arduino_Relay_Shield_v3_0.NO1, R4.Pin_0
  N6: Arduino_Relay_Shield_v3_0.NO2, Arduino_Relay_Shield_v3_0.COM3
  N7: Arduino_Relay_Shield_v3_0.NC2, Arduino_Relay_Shield_v3_0.COM4
  N8: Arduino_Relay_Shield_v3_0.NO3, R3.Pin_0
  N9: Arduino_Relay_Shield_v3_0.NC3, R2.Pin_0
  N10: Arduino_Relay_Shield_v3_0.NO4, R1.Pin_0
  N11: R1.Pin_1, LED1.anode
  N12: R2.Pin_1, LED2.anode
  N13: R3.Pin_1, LED3.anode
  N14: R4.Pin_1, LED4.anode

custom parts:
  SeeedStudio Relay Shield 2.1: SeeedStudio Relay Shield 2.x The Relay Shield provides a solution for controlling high current devices that cannot be controlled by the Arduino’s Digital I/O pins due to their current and voltage limits. The Relay Shield features four high quality relays and provides NO/NC interfaces, four dynamic LED indicators to show the on/off state of each relay, and the standardized shield form factor to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
